# Fritzing sketch elec291lab1 (saved by Fritzing 0.9.2b)
circuit board: 8.46667cm x 5.64444cm
breadboards: 1

parts:
  Part1 = Arduino Uno (Rev3)
  LED1 = RGB LED (com. cathode, rgb) [package="5 mm [THT]"]
  R1 = Resistor [tolerance=±5% resistance=220 package=THT]
  R2 = Resistor [tolerance=±5% resistance=220 package=THT]
  R3 = Resistor [tolerance=±5% resistance=220 package=THT]
  R4 = Resistor [tolerance=±5% resistance=220 package=THT]
  R6 = Resistor [tolerance=±5% resistance=220 package=THT]
  SW1 = DIP Switch 8 Position [package=dipswitch-08]
  LED2 = LED - 5mm [color="Red (633nm)" package="5 mm [THT]"]
  R8 = Photocell (LDR) [package=THT]
  resistor1 = Resistor [tolerance=±5% resistance=330 package=THT]
  resistor2 = Resistor [tolerance=±5% resistance=330 package=THT]

nets:
  N1: Part1.A2, R8.pin_0, resistor2.Pin_0
  N2: Part1.D11_PWM/MOSI, LED2.anode
  N3: Part1.GND, R4.Pin_0, R6.Pin_0, resistor1.Pin_1, resistor2.Pin_1
  N4: Part1.D1/TX, R6.Pin_1, SW1.16
  N5: Part1.D2, R4.Pin_1, SW1.15
  N6: Part1.D3_PWM, R1.Pin_1
  N7: Part1.D4, R3.Pin_1
  N8: Part1.D5_PWM, R2.Pin_1
  N9: Part1.5V, LED1.common_cathode, SW1.1, SW1.2, R8.pin_1
  N10: LED2.cathode, resistor1.Pin_0

// code stored in the sketch: lab1.ino
const int ledPin=13;
int ledState=LOW;
unsigned long previousMillis=0;
const long timeInterval= 2000;
void setup() {
  // put your setup code here, to run once:
pinMode(ledPin,OUTPUT);
}

void loop() {
  // put your main code here, to run repeatedly:
unsigned long currentMillis=millis();
if(currentMillis- previousMillis>= timeInterval){
 previousMillis=currentMillis;
 if(ledState==LOW){
  ledState=HIGH;
 }else{
  ledState=LOW;
 }
 digitalWrite(ledPin,ledState);
}

}
