# Fritzing sketch lab2 (saved by Fritzing 0.9.2b)
breadboards: 1

parts:
  Part1 = Arduino Uno (Rev3) - ICSP
  J1 = Piezo Speaker
  R1 = Resistor [tolerance=±5% resistance=330 package="2512 [SMD]"]
  R2 = Resistor [tolerance=±5% resistance=330 package="2512 [SMD]"]
  R3 = Resistor [tolerance=±20% resistance=330 package="2512 [SMD]"]
  R4 = Resistor [tolerance=±5% resistance=330 package="2512 [SMD]"]
  R5 = Resistor [tolerance=±5% resistance=330 package="2512 [SMD]"]
  R7 = Resistor [tolerance=±5% resistance=330 package="2512 [SMD]"]
  R10 = Resistor [tolerance=±5% resistance=330 package="2512 [SMD]"]
  7_Segment1 = 7 Segment Display
  R11 = Resistor [tolerance=±5% resistance=330 package="2512 [SMD]"]
  R12 = Resistor [tolerance=±5% resistance=330 package="0805 [SMD]"]
  R13 = Resistor [tolerance=±5% resistance=220 package=THT]
  LED1 = LEDs [package=led10mm]

nets:
  N1: Part1.D8, Part1.D4, R1.Pin_0, R1.Pin_1, R4.Pin_0, R4.Pin_1, 7_Segment1.common_anode
  N2: Part1.D9_PWM, R2.Pin_0, R2.Pin_1, 7_Segment1.Segment_E
  N3: Part1.D10_PWM/SS, R7.Pin_0, R7.Pin_1, 7_Segment1.Segment_D
  N4: Part1.D11_PWM/MOSI, R11.Pin_0
  N5: Part1.D13/SCK, R13.Pin_1
  N6: Part1.GND, J1.pin1, J1.pin2, R11.Pin_1, LED1.C
  N7: Part1.D2, R10.Pin_0, R10.Pin_1, 7_Segment1.Segment_A
  N8: Part1.D3_PWM, R5.Pin_0, R5.Pin_1, 7_Segment1.Segment_B
  N9: Part1.D5_PWM, 7_Segment1.Segment_C, R12.Pin_0, R12.Pin_1
  N10: Part1.D7, R3.Pin_0, R3.Pin_1, 7_Segment1.Segment_F
  N11: Part1.5V, 7_Segment1.Segment_DP
  N12: R13.Pin_0, LED1.A
