# Fritzing sketch fritzinglab3 (saved by Fritzing 0.9.2b)
breadboards: 1

parts:
  LCD1 = LCD screen
  Arduino1 = Arduino Uno (Rev3)
  KEYPAD1 = Membrane Matrix Keypad
  R2 = Trimmer Potentiometer [maximum_resistance=10kΩ package=THT]
  R3 = Resistor [tolerance=±5% resistance=220 package="0603 [SMD]"]

nets:
  N1: LCD1.VSS, LCD1.R/W, LCD1.LED-
  N2: LCD1.VDD, LCD1.LED+, R3.Pin_0
  N3: LCD1.V0, R2.wiper
  N4: LCD1.RS, Arduino1.A1
  N5: LCD1.E, Arduino1.D13/SCK
  N6: LCD1.DB4, Arduino1.D12/MISO
  N7: LCD1.DB5, Arduino1.D11_PWM/MOSI
  N8: LCD1.DB6, Arduino1.D10_PWM/SS
  N9: LCD1.DB7, Arduino1.D9_PWM
  N10: Arduino1.D8, KEYPAD1.1
  N11: Arduino1.D2, KEYPAD1.7
  N12: Arduino1.D3_PWM, KEYPAD1.6
  N13: Arduino1.D4, KEYPAD1.5
  N14: Arduino1.D5_PWM, KEYPAD1.4
  N15: Arduino1.D6_PWM, KEYPAD1.3
  N16: Arduino1.D7, KEYPAD1.2
  N17: Arduino1.5V, R3.Pin_1
  N18: Arduino1.GND, R2.leg1

custom parts:
  Membrane Matrix Keypad: Membrane Matrix 3x4 Keypad
