# Fritzing sketch lab4fritzing (saved by Fritzing 0.9.2b)
breadboards: 2

parts:
  Part1 = Arduino Uno (Rev3) - ICSP
  R1 = Trimmer Potentiometer [maximum_resistance=10kΩ package=THT]
  R2 = Photocell (LDR) [package=THT]
  R3 = Resistor [tolerance=±5% resistance=220 package="0603 [SMD]"]
  T1 = LM35 Temperature Sensor [package="TO92 [THT]"]
  R4 = Resistor [tolerance=±5% resistance=220 package="0603 [SMD]"]
  DHT1 = DHT11 Humitidy and Temperature Sensor
  R5 = Resistor [tolerance=±5% resistance=220 package="0603 [SMD]"]
  S1 = Square Pushbutton
  R6 = Resistor [tolerance=±5% resistance=220 package="0603 [SMD]"]

nets:
  N1: Part1.A0, R2.pin_0, R3.Pin_1
  N2: Part1.A1, T1.Vout, R4.Pin_0
  N3: Part1.5V, R1.wiper, R1.leg2, R3.Pin_0, T1.+Vs, R5.Pin_0
  GND: Part1.GND, R1.leg1, R2.pin_1, T1.GND, R4.Pin_1
  N4: Part1.D3_PWM, S1.leg0, R6.Pin_0
  N5: Part1.D7, DHT1.DATA, R5.Pin_1
  N6: DHT1.VDD, R6.Pin_1
  N7: DHT1.GND, S1.leg1

custom parts:
  DHT11 Humitidy and Temperature Sensor: DHT11 Humidity and Temperature Sensor
