# Fritzing sketch arduinoOscilloscope (saved by Fritzing 0.9.2b)
breadboards: 1

parts:
  Part2 = Arduino Uno (Rev3) - ICSP
  S1 = Round Pushbutton
  R1 = Resistor [tolerance=±5% resistance=220 package="0603 [SMD]"]

nets:
  N1: Part2.D3_PWM, S1.leg0, R1.Pin_1
  N2: Part2.5V, R1.Pin_0
  N3: Part2.GND, S1.leg1
